# Fritzing sketch PulseIn (saved by Fritzing 0.7.11b)
breadboards: 1

parts:
  S1 = Pushbutton [package=THT]
  R1 = Resistor [resistance=10k tolerance=±5% package=THT]
  Arduino2 = Arduino

nets:
  N1: S1.leg0, Arduino2.+5V
  N2: S1.leg1, R1.Pin_1, Arduino2.D2
  N3: R1.Pin_0, Arduino2.GND
