# Fritzing sketch SevenSegment (saved by Fritzing 0.7.11b)
breadboards: 1

parts:
  Arduino1 = Arduino
  7_Segment1 = 7 Segment Display
  U1 = 74HC595 [package="DIP16 [THT]"]
  R1 = 220 Ω Resistor [package=THT]
  R2 = 220 Ω Resistor [package=THT]
  R3 = 220 Ω Resistor [package=THT]
  R4 = 220 Ω Resistor [package=THT]
  R5 = 220 Ω Resistor [package=THT]
  R6 = 220 Ω Resistor [package=THT]
  R7 = 220 Ω Resistor [package=THT]
  R8 = 220 Ω Resistor [package=THT]

nets:
  GND: Arduino1.GND
  N1: Arduino1.D12, U1.MR
  N2: Arduino1.D11, U1.SH_CP
  N3: Arduino1.D10, U1.ST_CP
  N4: Arduino1.D9, U1.OE
  N5: Arduino1.D8, U1.DS
  5V: Arduino1.+5V, U1.VCC
  N6: 7_Segment1.Segment_A, R6.Pin_1
  N7: 7_Segment1.Segment_F, R7.Pin_1
  N8: 7_Segment1.common_cathode#3, 7_Segment1.common_cathode#5, 7_Segment1.common_cathode#11, 7_Segment1.common_cathode#16, U1.GND
  N9: 7_Segment1.Segment_E, R8.Pin_1
  N10: 7_Segment1.Segment_DP, R5.Pin_0
  N11: 7_Segment1.Segment_D, R4.Pin_0
  N12: 7_Segment1.common_cathode#12, R3.Pin_0
  N13: 7_Segment1.Segment_G, R2.Pin_0
  N14: 7_Segment1.Segment_B, R1.Pin_0
  N15: U1.Q4, R8.Pin_0
  N16: U1.Q5, R7.Pin_0

notes:
  A
  B
  C
  D
  E
  F
  G
  H

// code stored in the sketch: Shift_Register.ino
/*
  Shift Register Example
 for 74HC595 shift register

 This sketch turns reads serial input and uses it to set the pins
 of a 74HC595 shift register.

 Hardware:
 * 74HC595 shift register attached to pins 2, 3, and 4 of the Arduino,
 as detailed below.
 * LEDs attached to each of the outputs of the shift register

 Created 22 May 2009
 Created 23 Mar 2010
 by Tom Igoe

 */

//Pin connected to latch pin (ST_CP) of 74HC595
const int latchPin = 8;
//Pin connected to clock pin (SH_CP) of 74HC595
const int clockPin = 12;
////Pin connected to Data in (DS) of 74HC595
const int dataPin = 11;

void setup() {
  //set pins to output because they are addressed in the main loop
  pinMode(latchPin, OUTPUT);
  pinMode(dataPin, OUTPUT);  
  pinMode(clockPin, OUTPUT);
  Serial.begin(9600);
  Serial.println("reset");
}

void loop() {
  if (Serial.available() > 0) {
    // ASCII '0' through '9' characters are
    // represented by the values 48 through 57.
    // so if the user types a number from 0 through 9 in ASCII, 
    // you can subtract 48 to get the actual value:
    int bitToSet = Serial.read() - 48;

  // write to the shift register with the correct bit set high:
    registerWrite(bitToSet, HIGH);
  }
}

// This method sends bits to the shift register:

void registerWrite(int whichPin, int whichState) {
// the bits you want to send
  byte bitsToSend = 0;

  // turn off the output so the pins don't light up
  // while you're shifting bits:
  digitalWrite(latchPin, LOW);

  // turn on the next highest bit in bitsToSend:
  bitWrite(bitsToSend, whichPin, whichState);

  // shift the bits out:
  shiftOut(dataPin, clockPin, MSBFIRST, bitsToSend);

    // turn on the output so the LEDs can light up:
  digitalWrite(latchPin, HIGH);

}
