# Fritzing sketch Analog (saved by Fritzing 0.7.11b)
breadboards: 1

parts:
  LED2 = LED - 5mm [color="Red (633nm)" package="5 mm [THT]"]
  R1 = Rotary Potentiometer (Large) [maximum_resistance=100kΩ package=THT]
  Arduino2 = Arduino

nets:
  N1: LED2.cathode, R1.leg2, Arduino2.GND
  N2: LED2.anode, Arduino2.D13
  N3: R1.leg1, Arduino2.+5V
  N4: R1.wiper, Arduino2.A3
