# Fritzing sketch Servo (saved by Fritzing 0.7.11b)
breadboards: 1

parts:
  J1 = Basic Servo
  Arduino2 = Arduino

nets:
  GND: J1.gnd, Arduino2.GND
  VCC: J1.vcc, Arduino2.+5V
  N1: J1.pulse, Arduino2.D9
