# Fritzing sketch Blink (saved by Fritzing 0.7.11b)

parts:
  LED1 = LED - 5mm [color="Red (633nm)" package="5 mm [THT]"]
  Arduino2 = Arduino

nets:
  N1: LED1.cathode, Arduino2.GND
  N2: LED1.anode, Arduino2.D13
